# Fritzing sketch schematic (saved by Fritzing 0.9.3b)
breadboards: 1

parts:
  Part1 = Arduino Uno (Rev3)
  J1 = Basic Servo
  HC-SR04_Sensor_1 = HC-SR04 Ultrasonic Distance Sensor
  R1 = Resistor [tolerance=±5% resistance=370 package=THT]
  R2 = Resistor [tolerance=±5% resistance=440 package=THT]
  LED1 = LED - 5mm [color="Red (633nm)" package="5 mm [THT]"]

nets:
  N1: Part1.D11_PWM/MOSI, R1.Pin_0
  N2: Part1.D12/MISO, HC-SR04_Sensor_1.TRIG
  GND: Part1.GND, J1.gnd, HC-SR04_Sensor_1.GND, R2.Pin_1, LED1.anode
  N3: Part1.D3_PWM, LED1.cathode
  VCC: Part1.5V, J1.vcc, HC-SR04_Sensor_1.VCC
  N4: HC-SR04_Sensor_1.ECHO, R1.Pin_1, R2.Pin_0
